// Logisim project SingleCycleProcessor.circ as structural Verilog: 10 circuits, main circuit PROCESSOR
module logicUnit (
  input  [15:0] A,
  input  [15:0] B,
  input  [2:0] Func,
  output [15:0] R
);

  wire [15:0] and_1_out, nor_1_out, or_1_out, shifter_1_out, shifter_2_out, shifter_3_out, shifter_4_out,
       xor_1_out;

  assign and_1_out = B & A;  // AND_Gate and_1, 16 bits wide
  assign or_1_out = B | A;  // OR_Gate or_1, 16 bits wide
  assign nor_1_out = ~(B | A);  // NOR_Gate nor_1, 16 bits wide
  assign xor_1_out = B ^ A;  // XOR_Gate xor_1, 16 bits wide
  Shifter #(.width(16)) shifter_1 (.in(A), .\dist (B[3:0]), .out(shifter_1_out));
  Shifter #(.width(16), .shift("lr")) shifter_2 (.in(A), .\dist (B[3:0]), .out(shifter_2_out));
  Shifter #(.width(16), .shift("ar")) shifter_3 (.in(A), .\dist (B[3:0]), .out(shifter_3_out));
  Shifter #(.width(16), .shift("rl")) shifter_4 (.in(A), .\dist (B[3:0]), .out(shifter_4_out));
  Multiplexer #(.select(3), .width(16), .enable("false")) multiplexer_1 (
    .in0(and_1_out), .in1(or_1_out), .in2(nor_1_out), .in3(xor_1_out), .in4(shifter_1_out),
    .in5(shifter_2_out), .in6(shifter_3_out), .in7(shifter_4_out), .out(R), .sel(Func));
endmodule

module ArithUnit (
  input  [15:0] A,
  input  [15:0] B,
  input  [2:0] func,
  output zeroFlag,
  output [15:0] R
);

  wire comparator_1_eq, comparator_1_lt, comparator_2_eq, comparator_2_lt, or_1_out, or_2_out;
  wire [15:0] adder_1_out, bit_extender_1_out, bit_extender_2_out, bit_extender_3_out, bit_extender_4_out,
       subtractor_1_out;

  Comparator #(.width(16)) comparator_1 (.a(A), .b(B), .eq(comparator_1_eq), .lt(comparator_1_lt));  // open: gt
  Comparator #(.width(16), .mode("unsigned")) comparator_2 (
    .a(A), .b(B), .eq(comparator_2_eq), .lt(comparator_2_lt));  // open: gt
  Adder #(.width(16)) adder_1 (.a(A), .b(B), .out(adder_1_out), .cin(1'b0));  // open: cout
  Subtractor #(.width(16)) subtractor_1 (.a(A), .b(B), .out(subtractor_1_out), .bin(1'b0));  // open: bout
  or or_1 (or_1_out, comparator_2_eq, comparator_2_lt);
  or or_2 (or_2_out, comparator_1_eq, comparator_1_lt);
  assign bit_extender_1_out = {{15{1'b0}}, comparator_1_lt};  // Bit_Extender bit_extender_1
  assign bit_extender_2_out = {{15{1'b0}}, comparator_2_lt};  // Bit_Extender bit_extender_2
  assign bit_extender_3_out = {{15{1'b0}}, or_2_out};  // Bit_Extender bit_extender_3
  assign bit_extender_4_out = {{15{1'b0}}, or_1_out};  // Bit_Extender bit_extender_4
  Multiplexer #(.select(3), .width(16), .enable("false")) multiplexer_1 (
    .in0(adder_1_out), .in1(subtractor_1_out), .in2(bit_extender_1_out), .in3(bit_extender_2_out),
    .in4(bit_extender_3_out), .in5(bit_extender_4_out), .in6(A), .in7(A), .out(R), .sel(func));
  nor nor_1 (zeroFlag, subtractor_1_out[0], subtractor_1_out[1], subtractor_1_out[2], subtractor_1_out[3], subtractor_1_out[4], subtractor_1_out[5], subtractor_1_out[6], subtractor_1_out[7], subtractor_1_out[8], subtractor_1_out[9], subtractor_1_out[10], subtractor_1_out[11], subtractor_1_out[12], subtractor_1_out[13], subtractor_1_out[14], subtractor_1_out[15]);
endmodule

module ALU (
  input  [15:0] in_1,
  input  [15:0] in_2,
  input  [3:0] Code,
  output [15:0] out_4,
  output zeroFlag
);

  wire [15:0] arithunit_1_r, logicunit_1_r;

  logicUnit logicunit_1 (.R(logicunit_1_r), .A(in_1), .B(in_2), .Func(Code[3:1]));
  ArithUnit arithunit_1 (.A(in_1), .B(in_2), .zeroFlag(zeroFlag), .R(arithunit_1_r), .func(Code[3:1]));
  Multiplexer #(.width(16), .enable("false")) multiplexer_1 (
    .in0(logicunit_1_r), .in1(arithunit_1_r), .out(out_4), .sel(Code[0]));
endmodule

// ALU Control Unit
module ALUControlUnit (
  input  [2:0] Func,
  input  [2:0] ALUOp,
  output [3:0] out_3
);

  Multiplexer #(.select(3), .width(4), .enable("false")) multiplexer_1 (
    .in0({Func, 1'b0}), .in1({Func, 1'b1}), .in2(4'b0001), .in3(4'b0000), .in4(4'b0010), .out(out_3),
    .sel(ALUOp));  // open: in5, in6, in7
endmodule

module RegisterFile (
  input  clk,
  input  [15:0] Data,
  input  [2:0] A,
  input  Write,
  input  [2:0] Rd,
  input  [2:0] B,
  output [15:0] BusA,
  output [15:0] BusB,
  output [15:0] R0,
  output [15:0] R1,
  output [15:0] R2,
  output [15:0] R3,
  output [15:0] R4,
  output [15:0] R5,
  output [15:0] R6,
  output [15:0] R7
);

  wire demultiplexer_1_out0, demultiplexer_1_out1, demultiplexer_1_out2, demultiplexer_1_out3,
       demultiplexer_1_out4, demultiplexer_1_out5, demultiplexer_1_out6, demultiplexer_1_out7;

  Demultiplexer #(.select(3), .enable("false")) demultiplexer_1 (
    .out0(demultiplexer_1_out0), .out1(demultiplexer_1_out1), .out2(demultiplexer_1_out2),
    .out3(demultiplexer_1_out3), .out4(demultiplexer_1_out4), .out5(demultiplexer_1_out5),
    .out6(demultiplexer_1_out6), .out7(demultiplexer_1_out7), .in(Write), .sel(Rd));
  Register #(.width(16)) register_1 (.D({16{1'b0}}), .en(demultiplexer_1_out0), .Q(R0), .clk(clk));  // open: clr
  Register #(.width(16)) u_R1 (.D(Data), .en(demultiplexer_1_out1), .Q(R1), .clk(clk));  // open: clr
  Register #(.width(16)) u_R2 (.D(Data), .en(demultiplexer_1_out2), .Q(R2), .clk(clk));  // open: clr
  Register #(.width(16)) u_R3 (.D(Data), .en(demultiplexer_1_out3), .Q(R3), .clk(clk));  // open: clr
  Register #(.width(16)) u_R4 (.D(Data), .en(demultiplexer_1_out4), .Q(R4), .clk(clk));  // open: clr
  Register #(.width(16)) u_R5 (.D(Data), .en(demultiplexer_1_out5), .Q(R5), .clk(clk));  // open: clr
  Register #(.width(16)) u_R6 (.D(Data), .en(demultiplexer_1_out6), .Q(R6), .clk(clk));  // open: clr
  Register #(.width(16)) u_R7 (.D(Data), .en(demultiplexer_1_out7), .Q(R7), .clk(clk));  // open: clr
  Multiplexer #(.select(3), .width(16), .enable("false")) multiplexer_1 (
    .in0(R0), .in1(R1), .in2(R2), .in3(R3), .in4(R4), .in5(R5), .in6(R6), .in7(R7), .out(BusA), .sel(A));
  Multiplexer #(.select(3), .width(16), .enable("false")) multiplexer_2 (
    .in0(R0), .in1(R1), .in2(R2), .in3(R3), .in4(R4), .in5(R5), .in6(R6), .in7(R7), .out(BusB), .sel(B));
endmodule

// PC Value
module PC_Value (
  input  [15:0] busA,
  input  [1:0] PC2,
  input  [5:0] offset_br,
  input  clk,
  input  [11:0] jump_0_11,
  input  zero_flag,
  input  bne,
  input  beq,
  output [11:0] PC_plus_1,
  output [11:0] PC_value
);

  wire and_1_out, and_2_out, or_1_out;
  wire [11:0] adder_1_out, bit_extender_1_out, bit_extender_2_out, multiplexer_1_out, multiplexer_2_out;

  assign bit_extender_1_out = {{6{offset_br[5]}}, offset_br};  // Bit_Extender bit_extender_1
  Adder #(.width(12)) adder_1 (.a(bit_extender_1_out), .b(PC_plus_1), .out(adder_1_out));  // open: cin, cout
  Multiplexer #(.width(12), .enable("false")) multiplexer_1 (
    .in0(PC_plus_1), .in1(adder_1_out), .out(multiplexer_1_out), .sel(or_1_out));
  or or_1 (or_1_out, and_1_out, and_2_out);
  and and_1 (and_1_out, ~zero_flag, bne);  // AND_Gate
  and and_2 (and_2_out, zero_flag, beq);
  Bit_Extender #(.in_width(16), .out_width(12)) bit_extender_2 (.in(busA), .out(bit_extender_2_out));
  Multiplexer #(.select(2), .width(12), .enable("false")) multiplexer_2 (
    .in0(multiplexer_1_out), .in1(bit_extender_2_out), .in2(jump_0_11), .out(multiplexer_2_out), .sel(PC2));  // open: in3
  Register #(.width(12)) register_1 (.D(multiplexer_2_out), .Q(PC_value), .clk(clk));  // open: en, clr
  Adder #(.width(12)) adder_2 (.a(12'h1), .b(PC_value), .out(PC_plus_1));  // open: cin, cout
endmodule

// Control Unit
module ControlUnit (
  input  [3:0] op,
  input  [1:0] JRJARL,
  output [1:0] Rd,
  output sec,
  output [1:0] dest,
  output [2:0] ALUOp,
  output beq,
  output bne,
  output [1:0] pc2,
  output MemWrt,
  output MemRead,
  output RegWrt
);

  wire and_1_out, and_3_out, and_4_out, and_5_out, and_6_out, and_7_out, and_8_out, and_12_out, and_13_out,
       and_14_out, and_15_out, not_1_out, not_2_out, not_3_out, not_4_out, not_5_out, not_6_out, not_7_out,
       not_8_out, not_9_out, not_10_out, not_11_out, not_12_out, not_13_out, not_15_out, not_16_out,
       not_17_out, not_18_out, not_19_out, not_20_out;

  aluOP aluop_1 (.OP3(op[3]), .OP2(op[2]), .OP1(op[1]), .OP0(op[0]), .ALU2(ALUOp[2]), .ALU1(ALUOp[1]), .ALU0(ALUOp[0]));
  not not_1 (not_1_out, op[1]);
  not not_2 (not_2_out, JRJARL[1]);
  not not_3 (not_3_out, op[0]);
  and and_1 (and_1_out, op[3], op[1]);
  or or_1 (sec, op[1], op[3]);
  not not_4 (not_4_out, op[3]);
  not not_5 (not_5_out, op[1]);
  not not_6 (not_6_out, op[3]);
  not not_7 (not_7_out, op[1]);
  not not_8 (not_8_out, op[0]);
  not not_9 (not_9_out, op[1]);
  not not_10 (not_10_out, op[0]);
  not not_11 (not_11_out, op[1]);
  and and_2 (pc2[1], op[3], op[0]);
  or or_2 (pc2[0], JRJARL[1], JRJARL[0]);
  not not_12 (not_12_out, op[3]);
  not not_13 (not_13_out, op[2]);
  not not_14 (MemRead, op[0]);
  not not_15 (not_15_out, op[3]);
  not not_16 (not_16_out, op[2]);
  not not_17 (not_17_out, op[1]);
  not not_18 (not_18_out, JRJARL[0]);
  not not_19 (not_19_out, op[2]);
  not not_20 (not_20_out, op[0]);
  and and_3 (and_3_out, not_1_out, not_2_out);
  and and_4 (and_4_out, op[3], not_3_out);
  or or_3 (Rd[0], JRJARL[1], and_1_out);
  and and_5 (and_5_out, not_4_out, not_5_out);
  and and_6 (and_6_out, op[3], op[0]);
  and and_7 (and_7_out, not_6_out, not_7_out);
  and and_8 (and_8_out, op[3], op[1], not_8_out);
  and and_9 (beq, op[2], not_9_out, not_10_out);
  and and_10 (bne, op[2], not_11_out, op[0]);
  and and_11 (MemWrt, not_12_out, not_13_out, op[1], op[0]);
  and and_12 (and_12_out, not_15_out, not_16_out, not_17_out, not_18_out);
  and and_13 (and_13_out, not_19_out, not_20_out);
  and and_14 (and_14_out, op[2], op[1]);
  and and_15 (and_15_out, op[3], op[1]);
  or or_4 (Rd[1], and_3_out, op[2], and_4_out);
  or or_5 (dest[1], and_5_out, and_6_out);
  or or_6 (dest[0], and_7_out, and_8_out);
  or or_7 (RegWrt, and_12_out, and_13_out, and_14_out, and_15_out);
endmodule

module Jout2 (
  input  [3:0] Op,
  input  [2:0] Func,
  output [1:0] out_3
);

  wire not_1_out, not_2_out, not_3_out, not_4_out, not_5_out, not_6_out, not_7_out;

  not not_1 (not_1_out, Op[3]);
  not not_2 (not_2_out, Op[2]);
  not not_3 (not_3_out, Op[1]);
  not not_4 (not_4_out, Func[0]);
  not not_5 (not_5_out, Op[3]);
  not not_6 (not_6_out, Op[2]);
  not not_7 (not_7_out, Op[1]);
  and and_1 (out_3[0], not_1_out, not_2_out, not_3_out, Op[0], Func[2], Func[1], not_4_out);
  and and_2 (out_3[1], not_5_out, not_6_out, not_7_out, Op[0], Func[2], Func[1], Func[0]);
endmodule

module PROCESSOR (
  output [15:0] R1,
  output [15:0] R2,
  output [15:0] R3,
  output [15:0] R4,
  output [15:0] R5,
  output [15:0] R6,
  output [15:0] R7,
  output halt
);

  wire _0, _1, _2, _3, _4, _5, _6, _7, _8, _9, _10, _11, _12, _13, _14, _15, beq, bne, clk,
       controlunit_1_regwrt, MemRe, MemWrt, Sec, z_flagg;
  wire [1:0] Dest, jout2_1_out_3, PC2, Rd;
  wire [2:0] ALuOp, multiplexer_1_out;
  wire [3:0] alucontrolunit_1_out_3;
  wire [11:0] bit_extender_4_out, pc_value_1_pc_plus_1, pc_value_1_pc_value;
  wire [15:0] alu_1_out_4, bit_extender_2_out, bit_extender_3_out, jr, multiplexer_2_out, multiplexer_3_out,
       pc_plusOne, R0, ram_1_data, registerfile_1_busb, shifter_1_out;

  PC_Value pc_value_1 (
    .busA(jr), .PC2(PC2), .offset_br({_5, _4, _3, _2, _1, _0}),
    .jump_0_11({_11, _10, _9, _8, _7, _6, _5, _4, _3, _2, _1, _0}), .zero_flag(z_flagg), .bne(bne),
    .beq(beq), .PC_plus_1(pc_value_1_pc_plus_1), .PC_value(pc_value_1_pc_value), .clk(clk));
  assign pc_plusOne = {{4{1'b0}}, pc_value_1_pc_plus_1};  // Bit_Extender bit_extender_1
  nor nor_1 (halt, _15, _14, _13, _12, _11, _10, _9, _8, _6, _5, _4, _3, _2, _1, _7, _0);
  ROM #(.addrWidth(12), .dataWidth(16)) rom_1 (
    .addr(pc_value_1_pc_value), .data({_15, _14, _13, _12, _11, _10, _9, _8, _7, _6, _5, _4, _3, _2, _1, _0}));  // open: sel
  Multiplexer #(.select(2), .width(3), .enable("false")) multiplexer_1 (
    .in0({_8, _7, _6}), .in1(3'b001), .in2(3'b111), .in3({_5, _4, _3}), .out(multiplexer_1_out), .sel(Dest));
  Jout2 jout2_1 (.Op({_15, _14, _13, _12}), .Func({_2, _1, _0}), .out_3(jout2_1_out_3));
  assign bit_extender_2_out = {{4{1'b0}}, {_11, _10, _9, _8, _7, _6, _5, _4, _3, _2, _1, _0}};  // Bit_Extender bit_extender_2
  assign bit_extender_3_out = {{10{_5}}, {_5, _4, _3, _2, _1, _0}};  // Bit_Extender bit_extender_3
  Shifter #(.width(16)) shifter_1 (.in(bit_extender_2_out), .\dist (4'b0100), .out(shifter_1_out));
  RegisterFile registerfile_1 (
    .clk(clk), .Data(multiplexer_3_out), .Write(controlunit_1_regwrt), .Rd(multiplexer_1_out), .BusA(jr),
    .A({_11, _10, _9}), .BusB(registerfile_1_busb), .B({_8, _7, _6}), .R0(R0), .R1(R1), .R2(R2), .R3(R3),
    .R4(R4), .R5(R5), .R6(R6), .R7(R7));
  ALUControlUnit alucontrolunit_1 (.Func({_2, _1, _0}), .ALUOp(ALuOp), .out_3(alucontrolunit_1_out_3));
  ControlUnit controlunit_1 (
    .op({_15, _14, _13, _12}), .Rd(Rd), .sec(Sec), .JRJARL(jout2_1_out_3), .dest(Dest), .ALUOp(ALuOp),
    .beq(beq), .bne(bne), .pc2(PC2), .MemWrt(MemWrt), .MemRead(MemRe), .RegWrt(controlunit_1_regwrt));
  Multiplexer #(.width(16), .enable("false")) multiplexer_2 (
    .in0(registerfile_1_busb), .in1(bit_extender_3_out), .out(multiplexer_2_out), .sel(Sec));
  ALU alu_1 (
    .in_1(jr), .in_2(multiplexer_2_out), .Code(alucontrolunit_1_out_3), .out_4(alu_1_out_4),
    .zeroFlag(z_flagg));
  Bit_Extender #(.in_width(16), .out_width(12)) bit_extender_4 (.in(alu_1_out_4), .out(bit_extender_4_out));
  RAM #(.addrWidth(12), .dataWidth(16), .bus("separate")) ram_1 (
    .addr(bit_extender_4_out), .din(registerfile_1_busb), .data(ram_1_data), .str(MemWrt), .clk(clk),
    .ld(MemRe));  // open: sel, clr
  Multiplexer #(.select(2), .width(16), .enable("false")) multiplexer_3 (
    .in0(ram_1_data), .in1(pc_plusOne), .in2(alu_1_out_4), .in3(shifter_1_out), .out(multiplexer_3_out),
    .sel(Rd));

  // Other names for the same wires on the sheet: j[11:0] = {_11, _10, _9, _8, _7, _6, _5, _4, _3, _2, _1, _0};
  //   offset[5:0] = {_5, _4, _3, _2, _1, _0}

  // Notes on the sheet:
  //   contents of rom_1 (hex, n*v repeats v):
  //   a384 8354 35b 2040 2081 20c2 890a 1921 1520 14f2 4182 1290 403b 3100 b012 55c 1b68 403f 4e9 2040
  //   2285 22c6 4e0 3100 1e06
endmodule

module aluOP (
  input  OP3,
  input  OP2,
  input  OP1,
  input  OP0,
  output ALU2,
  output ALU1,
  output ALU0
);

  wire and_2_out, and_3_out, and_4_out, and_5_out, not_1_out, not_2_out, not_3_out, not_4_out;

  and and_1 (ALU2, OP2, OP0);
  not not_1 (not_1_out, OP2);
  not not_2 (not_2_out, OP0);
  not not_3 (not_3_out, OP1);
  not not_4 (not_4_out, OP0);
  and and_2 (and_2_out, not_1_out, OP1);
  and and_3 (and_3_out, OP2, not_2_out);
  and and_4 (and_4_out, not_3_out, OP0);
  and and_5 (and_5_out, OP2, not_4_out);
  or or_1 (ALU1, and_2_out, and_3_out, OP3);
  or or_2 (ALU0, and_4_out, and_5_out);
endmodule
